# Fritzing sketch banjo (saved by Fritzing 0.9.3b)
breadboards: 1

parts:
  BeagleBone1 = BeagleBone Black
  U1 = POT [package=pot_mammoth]
  S1 = Pushbutton [package="[THT]"]
  R1 = Photocell (LDR) [package=THT]
  R2 = Resistor [tolerance=±5% resistance=220 package=THT]

nets:
  N1: BeagleBone1.no_name_yet#32, U1.E, S1.Pin_3, S1.Pin_4, R1.pin_0
  N2: BeagleBone1.no_name_yet#33, R1.pin_1, R2.Pin_0
  N3: BeagleBone1.no_name_yet#34, U1.S, R2.Pin_1
  N4: BeagleBone1.no_name_yet#38, U1.A
  N5: BeagleBone1.no_name_yet#42, S1.Pin_1, S1.Pin_2

custom parts:
  BeagleBone Black: BeagleBone Black rev. A5B
