# Fritzing sketch schematics (saved by Fritzing 0.9.3b)
breadboards: 1

parts:
  BeagleBone1 = BeagleBone Black
  S1 = Pushbutton [package="[THT]"]
  LED2 = LED - 5mm [color="Yellow (595nm)" package="5 mm [THT]"]
  LED1 = LED - 3mm [color="Green (570nm)" package="3 mm [THT]"]
  LED3 = smd LED [color="Red (633nm)" package="0603 [SMD]"]
  R1 = Resistor [tolerance=±5% resistance=220 package=THT]
  R2 = Resistor [tolerance=±5% resistance=220 package=THT]
  R3 = Resistor [tolerance=±5% resistance=220 package=THT]

nets:
  N1: BeagleBone1.no_name_yet#1, S1.Pin_1, S1.Pin_2, LED2.anode, LED1.anode, LED3.anode
  N2: BeagleBone1.no_name_yet#14, LED3.cathode, R1.Pin_0
  N3: BeagleBone1.no_name_yet#22, LED2.cathode, R2.Pin_0
  N4: BeagleBone1.no_name_yet#27, S1.Pin_3, S1.Pin_4
  N5: BeagleBone1.no_name_yet#30, LED1.cathode, R3.Pin_0

custom parts:
  BeagleBone Black: BeagleBone Black rev. A5B
