# Fritzing sketch esquematico (saved by Fritzing 0.9.3b)
breadboards: 1

parts:
  BeagleBone1 = BeagleBone Black
  LED1 = LED - 5mm [color="Green (555nm)" package="5 mm [THT]"]
  LED2 = LED - 5mm [color="Red (633nm)" package="5 mm [THT]"]
  LED3 = LED - 5mm [color="Yellow (595nm)" package="5 mm [THT]"]
  R1 = Resistor [tolerance=±5% resistance=220 package=THT]
  R2 = Resistor [tolerance=±5% resistance=220 package=THT]
  R3 = Resistor [tolerance=±5% resistance=220 package=THT]

nets:
  N1: BeagleBone1.no_name_yet#5, LED1.anode, LED2.anode, LED3.anode
  N2: BeagleBone1.no_name_yet#12, R1.Pin_1
  N3: BeagleBone1.no_name_yet#15, R2.Pin_1
  N4: BeagleBone1.no_name_yet#42, R3.Pin_1
  N5: LED1.cathode, R1.Pin_0
  N6: LED2.cathode, R3.Pin_0
  N7: LED3.cathode, R2.Pin_0

custom parts:
  BeagleBone Black: BeagleBone Black rev. A5B
